# Fritzing sketch final CPE 301 (saved by Fritzing 0.9.10b)
breadboards: 3

parts:
  Water_Level_Sensor = Water Level Sensor
  Arduino4 = Arduino Mega 2560 (Rev3)
  DHT11 = KY-015 Temperature & Humidity Sensor Module [package="Breakout board"]
  LED9 = LED - 5mm [color="Blue (430nm)" current=0.030 package="5 mm [THT]"]
  LED10 = smd LED [color="Red (633nm)" package="1206 [SMD]"]
  LED11 = LED - 5mm [color="Yellow (595nm)" current=0.030 package="5 mm [THT]"]
  LED12 = smd LED [color="Green (570nm)" package="0603 [SMD]"]
  ON/OFF_button = Pushbutton [package="[THT]"]
  Reset_button = Pushbutton [package="[THT]"]
  R13 = Resistor [tolerance=±5% resistance=330 package="1206 [SMD]"]
  R14 = Resistor [tolerance=±5% resistance=330 package="1206 [SMD]"]
  R15 = Resistor [tolerance=±5% resistance=330 package="1206 [SMD]"]
  R16 = Resistor [tolerance=±5% resistance=330 package="1206 [SMD]"]
  R17 = Resistor [tolerance=±5% resistance=330 package="1206 [SMD]"]
  R18 = Resistor [tolerance=±5% resistance=330 package="1206 [SMD]"]
  LCD3 = LCD screen
  Fan_motor = DC Motor [voltage_(max)=6V voltage_(min)=3V]
  SM1 = 28BYJ-48 Stepper Motor [part_number=28BYJ-48]
  Driver1 = 28BYJ-48 Driver Module [part_number=ULN2003 package=THT]
  IC1 = L293D [package=THT]
  VCC1 = Battery block 9V
  Part1 = Real Time Clock Module - DS1307 RTC Breakout Board
  counter-clockwise_turn_button = Pushbutton [package="[THT]"]
  clockwise_turn_button = Pushbutton [package="[THT]"]
  R19 = Resistor [tolerance=±5% resistance=330 package="0805 [SMD]"]
  R20 = Resistor [tolerance=±5% resistance=330 package="0805 [SMD]"]

nets:
  N1: Water_Level_Sensor.SIG, Arduino4.A4
  5V: Water_Level_Sensor.VCC, Arduino4.5V, DHT11.Vin, ON/OFF_button.Pin_1, ON/OFF_button.Pin_2, Reset_button.Pin_1, Reset_button.Pin_2, LCD3.VDD, LCD3.LED+, IC1.0V, VCC1.-, Part1.5V, counter-clockwise_turn_button.Pin_1, counter-clockwise_turn_button.Pin_2, clockwise_turn_button.Pin_1, clockwise_turn_button.Pin_2
  GND: Water_Level_Sensor.GND, Arduino4.GND, DHT11.-, R13.Pin_1, R14.Pin_1, R15.Pin_0, R16.Pin_0, R17.Pin_0, R18.Pin_0, LCD3.VSS, LCD3.R/W, LCD3.LED-, Part1.GND, R19.Pin_1, R20.Pin_1
  N2: Arduino4.D21/SCL, Part1.SCL
  N3: Arduino4.D20/SDA, Part1.SDA
  N4: Arduino4.D13_PWM, R19.Pin_0
  N5: Arduino4.D12_PWM, R20.Pin_0
  N6: Arduino4.D11_PWM, Driver1.IN4
  N7: Arduino4.D10_PWM, Driver1.IN3
  N8: Arduino4.D9_PWM, Driver1.IN2
  N9: Arduino4.D8_PWM, Driver1.IN1
  N10: Arduino4.D3_PWM, IC1.In_2
  N11: Arduino4.D4_PWM, IC1.In_1
  N12: Arduino4.D5_PWM, IC1.Enable_1
  N13: Arduino4.D6_PWM, DHT11.S
  N14: Arduino4.D22, LCD3.V0
  N15: Arduino4.D24, LCD3.RS
  N16: Arduino4.D26, LCD3.E
  N17: Arduino4.D28, LCD3.DB4
  N18: Arduino4.D30, LCD3.DB5
  N19: Arduino4.D32, LCD3.DB6
  N20: Arduino4.D34, LCD3.DB7
  N21: Arduino4.D51, ON/OFF_button.Pin_3, ON/OFF_button.Pin_4, R17.Pin_1
  N22: Arduino4.D53, Reset_button.Pin_3, Reset_button.Pin_4, R18.Pin_1
  N23: LED9.cathode, R13.Pin_0
  N24: LED10.cathode, R14.Pin_0
  N25: LED11.cathode, R15.Pin_1
  N26: LED12.cathode, R16.Pin_1
  N27: Fan_motor.pin_1, IC1.Out_2_(_Controlled_by_Enable_1_)
  N28: Fan_motor.pin_2, IC1.Out_1_(_Controlled_by_Enable_1_)
  N29: SM1.blue-pin, Driver1.blue-pin
  N30: SM1.pink-pin, Driver1.pink-pin
  N31: SM1.yellow-pin, Driver1.yellow-pin
  N32: SM1.orange-pin, Driver1.orange-pin
  N33: SM1.red-pin, Driver1.red-pin
  N34: IC1.+Vmotor, VCC1.+

custom parts:
  Water Level Sensor: A water level sensor. This sensor operates at 3V to 5V. The Sig (signal) pin outputs an analogue signal that is in proportion to the amount of water in contact with the sensor.
  KY-015 Temperature & Humidity Sensor Module: KY-015 temperature and humidity sensor module, provides a low-latency serial interface to measure humidity and temperature.
  28BYJ-48 Stepper Motor: Unipolar Stepper Motor 28BYJ-48 Top coil - pink & orange Bottom coil - blue & yellow Common rail - red Connector pins: blue - pink - yellow - orange - red
  28BYJ-48 Driver Module: ULN2003 Driver Module for the 28BYJ-48 Unipolar Stepper Motor LED A - Blue wire - Bottom coil left LED B - Pink wire - Top coil left LED C - Yellow wire - Bottom coil right LED D - Orange wire - Top coil right Common rail - red Connector pins: blue - pink - yellow - orange - red Control pins - IN1 to IN4 Power pins - GND & Vmotor (5-12V) On/Off jumper (if removed, power to motor is cut).
